# Fritzing sketch Rx (saved by Fritzing 0.9.3b)

parts:
  Part2 = NRF24L01+ Breakout Board
  Part5 = Arduino Nano (Rev3.0)
  R1 = Resistor [tolerance=±5% resistance=220 package=THT]
  R2 = Resistor [tolerance=±5% resistance=220 package=THT]
  R3 = Resistor [tolerance=±5% resistance=220 package=THT]
  R4 = Resistor [tolerance=±5% resistance=220 package=THT]
  LED1 = LED - 5mm [color="Red (633nm)" package="5 mm [THT]"]
  LED2 = LED - 5mm [color="Red (633nm)" package="5 mm [THT]"]
  LED3 = LED - 5mm [color="Red (633nm)" package="5 mm [THT]"]
  LED4 = LED - 5mm [color="Red (633nm)" package="5 mm [THT]"]

nets:
  GND: Part2.GND, Part5.GND, LED1.cathode, LED2.cathode, LED3.cathode, LED4.cathode
  VCC: Part2.VCC, Part5.3V3
  N1: Part2.CE, Part5.D9
  N2: Part2.CS, Part5.D10
  N3: Part2.SCK, Part5.D13/SCK
  N4: Part2.MOSI, Part5.D11/MOSI
  N5: Part2.MISO, Part5.D12/MISO
  N6: Part5.D2, R1.Pin_0
  N7: Part5.D3, R2.Pin_0
  N8: Part5.D4, R3.Pin_0
  N9: Part5.D5, R4.Pin_0
  N10: R1.Pin_1, LED1.anode
  N11: R2.Pin_1, LED2.anode
  N12: R3.Pin_1, LED3.anode
  N13: R4.Pin_1, LED4.anode
